// Logisim project CSE332_Rahiq_Tazrian.circ as structural Verilog
module _1_bit_ALU (
  input  A,
  input  B,
  input  CarryIn,
  input  [1:0] S1S0,
  output Result,
  output Cout
);

  wire adder_1_out, and_1_out, and_2_out, multiplexer_1_out, not_1_out, or_1_out;

  Multiplexer #(.enable("false")) multiplexer_1 (.in0(B), .in1(not_1_out), .out(multiplexer_1_out), .sel(and_1_out));
  not not_1 (not_1_out, B);
  and and_1 (and_1_out, S1S0[0], S1S0[1]);
  and and_2 (and_2_out, A, B);
  or or_1 (or_1_out, A, B);
  Adder #(.width(1)) adder_1 (.a(A), .b(multiplexer_1_out), .out(adder_1_out), .cin(CarryIn), .cout(Cout));
  Multiplexer #(.select(2), .enable("false")) multiplexer_2 (
    .in0(and_2_out), .in1(or_1_out), .in2(adder_1_out), .in3(adder_1_out), .out(Result), .sel(S1S0));
endmodule

module _32_bit_ALU (
  input  CarryIn,
  input  [15:0] A,
  input  [15:0] B,
  input  [1:0] S1S0,
  output [15:0] Result,
  output Cout
);

  wire main_1_cout, main_2_cout, main_3_cout, main_4_cout, main_5_cout, main_6_cout, main_7_cout,
       main_8_cout, main_9_cout, main_10_cout, main_11_cout, main_12_cout, main_13_cout, main_14_cout,
       main_15_cout;

  Lab_6_16_bit_alu_main main_1 (
    .A(A[0]), .B(B[0]), .CarryIn(CarryIn), .S1S0(S1S0), .Result(Result[0]), .Cout(main_1_cout));
  Lab_6_16_bit_alu_main main_2 (
    .A(A[1]), .B(B[1]), .CarryIn(main_1_cout), .S1S0(S1S0), .Result(Result[1]), .Cout(main_2_cout));
  Lab_6_16_bit_alu_main main_3 (
    .A(A[2]), .B(B[2]), .CarryIn(main_2_cout), .S1S0(S1S0), .Result(Result[2]), .Cout(main_3_cout));
  Lab_6_16_bit_alu_main main_4 (
    .A(A[3]), .B(B[3]), .CarryIn(main_3_cout), .S1S0(S1S0), .Result(Result[3]), .Cout(main_4_cout));
  Lab_6_16_bit_alu_main main_5 (
    .A(A[4]), .B(B[4]), .CarryIn(main_4_cout), .S1S0(S1S0), .Result(Result[4]), .Cout(main_5_cout));
  Lab_6_16_bit_alu_main main_6 (
    .A(A[5]), .B(B[5]), .CarryIn(main_5_cout), .S1S0(S1S0), .Result(Result[5]), .Cout(main_6_cout));
  Lab_6_16_bit_alu_main main_7 (
    .A(A[6]), .B(B[6]), .CarryIn(main_6_cout), .S1S0(S1S0), .Result(Result[6]), .Cout(main_7_cout));
  Lab_6_16_bit_alu_main main_8 (
    .A(A[7]), .B(B[7]), .CarryIn(main_7_cout), .S1S0(S1S0), .Result(Result[7]), .Cout(main_8_cout));
  Lab_6_16_bit_alu_main main_9 (
    .A(A[8]), .B(B[8]), .CarryIn(main_8_cout), .S1S0(S1S0), .Result(Result[8]), .Cout(main_9_cout));
  Lab_6_16_bit_alu_main main_10 (
    .A(A[9]), .B(B[9]), .CarryIn(main_9_cout), .S1S0(S1S0), .Result(Result[9]), .Cout(main_10_cout));
  Lab_6_16_bit_alu_main main_11 (
    .A(A[10]), .B(B[10]), .CarryIn(main_10_cout), .S1S0(S1S0), .Result(Result[10]), .Cout(main_11_cout));
  Lab_6_16_bit_alu_main main_12 (
    .A(A[11]), .B(B[11]), .CarryIn(main_11_cout), .S1S0(S1S0), .Result(Result[11]), .Cout(main_12_cout));
  Lab_6_16_bit_alu_main main_13 (
    .A(A[12]), .B(B[12]), .CarryIn(main_12_cout), .S1S0(S1S0), .Result(Result[12]), .Cout(main_13_cout));
  Lab_6_16_bit_alu_main main_14 (
    .A(A[13]), .B(B[13]), .CarryIn(main_13_cout), .S1S0(S1S0), .Result(Result[13]), .Cout(main_14_cout));
  Lab_6_16_bit_alu_main main_15 (
    .A(A[14]), .B(B[14]), .CarryIn(main_14_cout), .S1S0(S1S0), .Result(Result[14]), .Cout(main_15_cout));
  Lab_6_16_bit_alu_main main_16 (
    .A(A[15]), .B(B[15]), .CarryIn(main_15_cout), .S1S0(S1S0), .Result(Result[15]), .Cout(Cout));
endmodule

module _32_bit_RF (
  input  [15:0] Data_In,
  input  Reg_Write,
  input  [3:0] Read_Address_1,
  input  [3:0] Write_Address,
  input  [3:0] Read_Address_2,
  output [15:0] Data_Out_1,
  output [15:0] Data_Out_2
);

  wire and_1_out, and_2_out, and_3_out, and_4_out, and_5_out, and_6_out, and_7_out, and_8_out, and_9_out,
       and_10_out, and_11_out, and_12_out, and_13_out, and_14_out, and_15_out, and_16_out, decoder_1_out0,
       decoder_1_out1, decoder_1_out2, decoder_1_out3, decoder_1_out4, decoder_1_out5, decoder_1_out6,
       decoder_1_out7, decoder_1_out8, decoder_1_out9, decoder_1_out10, decoder_1_out11, decoder_1_out12,
       decoder_1_out13, decoder_1_out14, decoder_1_out15, undriven, undriven_2, undriven_3, undriven_4,
       undriven_5, undriven_6, undriven_7, undriven_8, undriven_9, undriven_10, undriven_11, undriven_12,
       undriven_13, undriven_14, undriven_15, undriven_16;
  wire [15:0] register_1_q, register_2_q, register_3_q, register_4_q, register_5_q, register_6_q,
       register_7_q, register_8_q, register_9_q, register_10_q, register_11_q, register_12_q, register_13_q,
       register_14_q, register_15_q, register_16_q;

  Decoder #(.select(4)) decoder_1 (
    .out0(decoder_1_out0), .out1(decoder_1_out1), .out2(decoder_1_out2), .out3(decoder_1_out3),
    .out4(decoder_1_out4), .out5(decoder_1_out5), .out6(decoder_1_out6), .out7(decoder_1_out7),
    .out8(decoder_1_out8), .out9(decoder_1_out9), .out10(decoder_1_out10), .out11(decoder_1_out11),
    .out12(decoder_1_out12), .out13(decoder_1_out13), .out14(decoder_1_out14), .out15(decoder_1_out15),
    .sel(Write_Address));  // open: en
  and and_1 (and_1_out, decoder_1_out0, Reg_Write);
  and and_2 (and_2_out, decoder_1_out1, Reg_Write);
  and and_3 (and_3_out, decoder_1_out2, Reg_Write);
  and and_4 (and_4_out, decoder_1_out3, Reg_Write);
  and and_5 (and_5_out, decoder_1_out4, Reg_Write);
  and and_6 (and_6_out, decoder_1_out5, Reg_Write);
  and and_7 (and_7_out, decoder_1_out6, Reg_Write);
  and and_8 (and_8_out, decoder_1_out7, Reg_Write);
  and and_9 (and_9_out, decoder_1_out8, Reg_Write);
  and and_10 (and_10_out, decoder_1_out9, Reg_Write);
  and and_11 (and_11_out, decoder_1_out10, Reg_Write);
  and and_12 (and_12_out, decoder_1_out11, Reg_Write);
  and and_13 (and_13_out, decoder_1_out12, Reg_Write);
  and and_14 (and_14_out, decoder_1_out13, Reg_Write);
  and and_15 (and_15_out, decoder_1_out14, Reg_Write);
  and and_16 (and_16_out, decoder_1_out15, Reg_Write);
  Register #(.width(16)) register_1 (.D(Data_In), .en(and_1_out), .Q(register_1_q), .clk(undriven));  // open: clr
  Register #(.width(16)) register_2 (.D(Data_In), .en(and_2_out), .Q(register_2_q), .clk(undriven));  // open: clr
  Register #(.width(16)) register_3 (.D(Data_In), .en(and_3_out), .Q(register_3_q), .clk(undriven));  // open: clr
  Register #(.width(16)) register_4 (.D(Data_In), .en(and_4_out), .Q(register_4_q), .clk(undriven));  // open: clr
  Register #(.width(16)) register_5 (.D(Data_In), .en(and_5_out), .Q(register_5_q), .clk(undriven));  // open: clr
  Register #(.width(16)) register_6 (.D(Data_In), .en(and_6_out), .Q(register_6_q), .clk(undriven));  // open: clr
  Register #(.width(16)) register_7 (.D(Data_In), .en(and_7_out), .Q(register_7_q), .clk(undriven));  // open: clr
  Register #(.width(16)) register_8 (.D(Data_In), .en(and_8_out), .Q(register_8_q), .clk(undriven));  // open: clr
  Register #(.width(16)) register_9 (.D(Data_In), .en(and_9_out), .Q(register_9_q));  // open: clk, clr
  Register #(.width(16)) register_10 (.D(Data_In), .en(and_10_out), .Q(register_10_q), .clk(undriven));  // open: clr
  Register #(.width(16)) register_11 (.D(Data_In), .en(and_11_out), .Q(register_11_q), .clk(undriven));  // open: clr
  Register #(.width(16)) register_12 (.D(Data_In), .en(and_12_out), .Q(register_12_q), .clk(undriven));  // open: clr
  Register #(.width(16)) register_13 (.D(Data_In), .en(and_13_out), .Q(register_13_q), .clk(undriven));  // open: clr
  Register #(.width(16)) register_14 (.D(Data_In), .en(and_14_out), .Q(register_14_q), .clk(undriven));  // open: clr
  Register #(.width(16)) register_15 (.D(Data_In), .en(and_15_out), .Q(register_15_q), .clk(undriven));  // open: clr
  Register #(.width(16)) register_16 (.D(Data_In), .en(and_16_out), .Q(register_16_q), .clk(undriven));  // open: clr
  Register #(.width(16)) register_17 (.D(Data_In), .clk(undriven_2));  // open: en, Q, clr
  Register #(.width(16)) register_18 (.D(Data_In), .clk(undriven_3));  // open: en, Q, clr
  Register #(.width(16)) register_19 (.D(Data_In), .clk(undriven_4));  // open: en, Q, clr
  Register #(.width(16)) register_20 (.D(Data_In), .clk(undriven_5));  // open: en, Q, clr
  Register #(.width(16)) register_21 (.D(Data_In), .clk(undriven_6));  // open: en, Q, clr
  Register #(.width(16)) register_22 (.D(Data_In), .clk(undriven_7));  // open: en, Q, clr
  Register #(.width(16)) register_23 (.D(Data_In), .clk(undriven_8));  // open: en, Q, clr
  Register #(.width(16)) register_24 (.D(Data_In), .clk(undriven_9));  // open: en, Q, clr
  Register #(.width(16)) register_25 (.D(Data_In));  // open: en, Q, clk, clr
  Register #(.width(16)) register_26 (.D(Data_In), .clk(undriven_10));  // open: en, Q, clr
  Register #(.width(16)) register_27 (.D(Data_In), .clk(undriven_11));  // open: en, Q, clr
  Register #(.width(16)) register_28 (.D(Data_In), .clk(undriven_12));  // open: en, Q, clr
  Register #(.width(16)) register_29 (.D(Data_In), .clk(undriven_13));  // open: en, Q, clr
  Register #(.width(16)) register_30 (.clk(undriven_14));  // open: D, en, Q, clr
  Register #(.width(16)) register_31 (.clk(undriven_15));  // open: D, en, Q, clr
  Register #(.width(16)) register_32 (.clk(undriven_16));  // open: D, en, Q, clr
  Multiplexer #(.select(4), .width(16), .enable("false")) multiplexer_1 (
    .in0(register_1_q), .in1(register_2_q), .in2(register_3_q), .in3(register_4_q), .in4(register_5_q),
    .in5(register_6_q), .in6(register_7_q), .in7(register_8_q), .in8(register_9_q), .in9(register_10_q),
    .in10(register_11_q), .in11(register_12_q), .in12(register_13_q), .in13(register_14_q),
    .in14(register_15_q), .in15(register_16_q), .out(Data_Out_1), .sel(Read_Address_1));
  Multiplexer #(.select(4), .width(16), .enable("false")) multiplexer_2 (
    .in0(register_1_q), .in1(register_2_q), .in2(register_3_q), .in3(register_4_q), .in4(register_5_q),
    .in5(register_6_q), .in6(register_7_q), .in7(register_8_q), .in8(register_9_q), .in9(register_10_q),
    .in10(register_11_q), .in11(register_12_q), .in12(register_13_q), .in13(register_14_q),
    .in14(register_15_q), .in15(register_16_q), .out(Data_Out_2), .sel(Read_Address_2));
endmodule
